# Fritzing sketch LED_control (saved by Fritzing 0.8.5b)
breadboards: 1

parts:
  R1 = Trimmer Potentiometer [maximum_resistance=10kΩ package=THT]
  R2 = Trimmer Potentiometer [maximum_resistance=10kΩ package=THT]
  R3 = Trimmer Potentiometer [maximum_resistance=10kΩ package=THT]
  C1 = Electrolytic Capacitor [capacitance=1µF package="100 mil [THT, electrolytic]"]
  C2 = Electrolytic Capacitor [capacitance=1µF package="100 mil [THT, electrolytic]"]
  C3 = Electrolytic Capacitor [capacitance=1µF package="100 mil [THT, electrolytic]"]
  LED1 = RGB LED (com. anode, rbg) [package="5 mm [THT]"]
  R4 = Resistor [tolerance=±5% resistance=220 package=THT]  # not connected
  R5 = Resistor [tolerance=±5% resistance=220 package=THT]  # not connected
  R6 = Resistor [tolerance=±5% resistance=220 package=THT]  # not connected
  Part1 = Arduino Uno (Rev3)

nets:
  N1: R1.leg1, R2.leg1, R3.leg1, C1.+, C2.+, C3.+, Part1.5V
  N2: R1.wiper, Part1.A2
  N3: R1.leg2, R2.leg2, R3.leg2, C1.-, C2.-, C3.-, LED1.common_anode, Part1.GND
  N4: R2.wiper, Part1.A1
  N5: R3.wiper, Part1.A0
